# Fritzing sketch FuseDoctor_Master_Attiny85 (saved by Fritzing 0.9.3b)
stripboards: 1

parts:
  U1 = attiny85 [package=dip]
  J4 = female pin header, 4 pins [form="♀ (female)"]
  J5 = female pin header, 4 pins [form="♀ (female)"]
  R1 = Resistor [tolerance=±5% resistance=1k package=THT]
  J1 = Power Jack [part_number="+12 vdc" package=power_jack_slot]
  R2 = Resistor [tolerance=±5% resistance=1k package=THT]
  U2 = attiny85 [package=dip]
  J6 = female pin header, 4 pins [form="♀ (female)"]
  J3 = female pin header, 4 pins [form="♀ (female)"]
  Q1 = NPN-Transistor [V] [part_number=2N3904 package="TO92 [THT]"]
  LED1 = LED - 3mm [color="Blue (470nm)" package="3 mm [THT]"]
  S1 = Pushbutton [package="[SMD]"]
  J2 = female pin header, 3 pins [form="♀ (female)"]
  IC1 = Voltage Regulator [part_number=LM7805 package=78xxl]
  R3 = Resistor [tolerance=±5% resistance=1k package=THT]
  C1 = Electrolytic Capacitor [capacitance=10µF voltage=35V package="100 mil [THT, electrolytic]"]
  C2 = Capacitor [part_number=103 package=cap-pth-small2]

nets:
  N1: U1.Pin_1, R1.Pin_1, J3.pin1, Q1.C
  N2: U1.Pin_2, J5.pin2, R2.Pin_0, U2.Pin_2, J3.pin2, J2.pin1
  N3: U1.Pin_3, J3.pin3
  GND: U1.Pin_4, J5.pin4, J1.GND, U2.Pin_4, J3.pin4, Q1.E, LED1.cathode, J2.pin2, IC1.GND, C1.-, C2.2
  N4: U1.Pin_5, J4.pin4, U2.Pin_5, J6.pin4
  N5: U1.Pin_6, J4.pin3, U2.Pin_6, J6.pin3
  N6: U1.Pin_7, J4.pin2, U2.Pin_7, J6.pin2
  N7: U1.Pin_8, J4.pin1, U2.Pin_8, J6.pin1, J2.pin3, IC1.OUT, C1.+, C2.1
  N8: J5.pin1, U2.Pin_1
  N9: J5.pin3, U2.Pin_3, R3.Pin_0
  N10: R1.Pin_0, S1.Pin_1, S1.Pin_2, IC1.IN
  N11: J1.PWR, S1.Pin_3, S1.Pin_4
  N12: R2.Pin_1, LED1.anode
  N13: Q1.B, R3.Pin_1

notes:
  Master
  Target
  12 vdc
  TX data

custom parts:
  Power Jack: Power Jack This is the standard 5.5mm barrel jack for power. The PTH is the most common, proven, reliable, footprint. All others are experimental. The Slot footprint only works if the mill layer is transmitted to the PCB fab house so be warned. Spark Fun Electronics SKU : PRT-00119. Mating wall wart : TOL-00298 (and others)
  NPN-Transistor [V]: A standard NPN-transistor

// code stored in the sketch: fuse_doctor_attiny85.ino
// AVR High-voltage Serial Fuse Reprogrammer
// Adapted from code and design by Paul Willoughby 03/20/2010
//   http://www.rickety.us/2010/03/arduino-avr-high-voltage-serial-programmer/
// and Wayne Holder 
//   https://sites.google.com/site/wayneholder/attiny-fuse-reset
//
// Fuse Calc:
//   http://www.engbedded.com/fusecalc/

#define  LED      3    // Status indicator LED
#define  RST      4    // (13) Output to level shifter for !RESET from transistor
#define  SCI      3    // (12) Target Clock Input
#define  SDO      2    // (11) Target Data Output
#define  SII      1    // (10) Target Instruction Input
#define  SDI      0    // ( 9) Target Data Input

#define  HFUSE  0x747C
#define  LFUSE  0x646C
#define  EFUSE  0x666E

// ATTiny series signatures
#define  ATTINY13   0x9007  // L: 0x6A, H: 0xFF             8 pin
#define  ATTINY24   0x910B  // L: 0x62, H: 0xDF, E: 0xFF   14 pin
#define  ATTINY25   0x9108  // L: 0x62, H: 0xDF, E: 0xFF    8 pin
#define  ATTINY44   0x9207  // L: 0x62, H: 0xDF, E: 0xFFF  14 pin
#define  ATTINY45   0x9206  // L: 0x62, H: 0xDF, E: 0xFF    8 pin
#define  ATTINY84   0x930C  // L: 0x62, H: 0xDF, E: 0xFFF  14 pin
#define  ATTINY85   0x930B  // L: 0x62, H: 0xDF, E: 0xFF    8 pin

int error = 0;
byte FuseH = 0;
byte FuseL = 0; 
byte FuseX = 0;

void setup() {
  pinMode(RST, OUTPUT);
  digitalWrite(RST, HIGH);  // Level shifter is inverting, this shuts off 12V
  pinMode(SDI, OUTPUT);
  pinMode(SII, OUTPUT);
  pinMode(SCI, OUTPUT);
  pinMode(SDO, OUTPUT);     // Configured as input when in programming mode

  digitalWrite(SDI, LOW);
  digitalWrite(SII, LOW);
  digitalWrite(SDO, LOW);

  delayMicroseconds(30);  // wait long enough for target chip to see rising edge
  digitalWrite(RST, LOW);  // 12v On
  delayMicroseconds(10);
  pinMode(SDO, INPUT);      // Set SDO to input
  delayMicroseconds(300);
  unsigned int sig = readSignature();

  if (sig == ATTINY13) {
    writeFuse(LFUSE, 0x6A);
    writeFuse(HFUSE, 0xFF);
    readFuses();    // check to make sure fuses were set properly
    if (FuseL != 0x6A || FuseH != 0xFF) {
      error = 5;    // fast flash if fuses don't match expected
    }
  } else if (sig == ATTINY24 || sig == ATTINY44 || sig == ATTINY84 ||
             sig == ATTINY25 || sig == ATTINY45 || sig == ATTINY85) {
    writeFuse(LFUSE, 0x62);
    writeFuse(HFUSE, 0xDF);
    writeFuse(EFUSE, 0xFF);
    readFuses();    // check to make sure fuses were set properly    
    if (FuseL != 0x62 || FuseH != 0xDF || FuseX != 0xFF) {
      error = 5;    // fast flash if fuses don't match expected
    }
  } else {    
    error = 1;      // slow flash if device signature is invalid
  }

  digitalWrite(SCI, LOW);
  digitalWrite(RST, HIGH);   // 12v Off
  digitalWrite(LED, LOW);    // LED off for succerss
}

void loop() {
  // Flash LED if there was an error
  while (error > 0) {
    int d = 500 / error;
    digitalWrite(LED, HIGH);
    delay(d);
    digitalWrite(LED, LOW);
    delay(d);
  }
}

byte shiftOut (byte val1, byte val2) {
  int inBits = 0;
  //Wait until SDO goes high
  while (!digitalRead(SDO))
    ;
  unsigned int dout = (unsigned int) val1 << 2;
  unsigned int iout = (unsigned int) val2 << 2;
  for (int ii = 10; ii >= 0; ii--)  {
    digitalWrite(SDI, !!(dout & (1 << ii)));
    digitalWrite(SII, !!(iout & (1 << ii)));
    inBits <<= 1;
    inBits |= digitalRead(SDO);
    digitalWrite(SCI, HIGH);
    digitalWrite(SCI, LOW);
  }
  return inBits >> 2;
}

void writeFuse (unsigned int fuse, byte val) {
  shiftOut(0x40, 0x4C);
  shiftOut( val, 0x2C);
  shiftOut(0x00, (byte) (fuse >> 8));
  shiftOut(0x00, (byte) fuse);
}

void readFuses () {
  shiftOut(0x04, 0x4C);  // LFuse
  shiftOut(0x00, 0x68);
  FuseL = shiftOut(0x00, 0x6C);

  shiftOut(0x04, 0x4C);  // HFuse
  shiftOut(0x00, 0x7A);
  FuseH = shiftOut(0x00, 0x7E);

  shiftOut(0x04, 0x4C);  // EFuse
  shiftOut(0x00, 0x6A);
  FuseX = shiftOut(0x00, 0x6E);
}

unsigned int readSignature () {
  unsigned int sig = 0;
  byte val;
  for (int ii = 1; ii < 3; ii++) {
    shiftOut(0x08, 0x4C);
    shiftOut(  ii, 0x0C);
    shiftOut(0x00, 0x68);
    val = shiftOut(0x00, 0x6C);
    sig = (sig << 8) + val;
  }
  return sig;
}
