# Fritzing sketch Fuse_Doctor (saved by Fritzing 0.9.3b)
stripboards: 2

parts:
  J1 = Power Jack [part_number="+12 vdc" package=power_jack_slot]
  R1 = Resistor [tolerance=±5% resistance=1k package=THT]
  Q1 = NPN-Transistor [part_number=2N3904 package="TO92 [THT]"]
  U1 = attiny85 [part_number=tiny_SOCKET package=dip]
  R2 = Resistor [tolerance=±5% resistance=1k package=THT]
  R3 = Resistor [tolerance=±5% resistance=1k package=THT]
  R4 = Resistor [tolerance=±5% resistance=1k package=THT]
  R5 = Resistor [tolerance=±5% resistance=1k package=THT]
  R6 = Resistor [tolerance=±5% resistance=1k package=THT]
  J2 = male pin header, 7 pins [form="♂ (male)"]
  J3 = Power Jack [part_number="+12 vdc" package=power_jack_slot]  # not connected

nets:
  N1: J1.GND, Q1.E, U1.Pin_4, J2.pin7
  N2: J1.PWR, R1.Pin_1
  N3: R1.Pin_0, Q1.C, U1.Pin_1
  N4: Q1.B, R4.Pin_1
  N5: U1.Pin_2, R6.Pin_1
  N6: U1.Pin_5, R2.Pin_1
  N7: U1.Pin_6, R3.Pin_1
  N8: U1.Pin_7, R5.Pin_1
  N9: U1.Pin_8, J2.pin1
  N10: R2.Pin_0, J2.pin2
  N11: R3.Pin_0, J2.pin3
  N12: R4.Pin_0, J2.pin6
  N13: R5.Pin_0, J2.pin4
  N14: R6.Pin_0, J2.pin5

notes:
  D8
  D9
  D10
  D11
  D12
  D13
  GND
  traces cuts
  parts top view
  traces on back side
  Jack mounted on board
  2N3904
  E B C
  8 pins dip socket
  1
  O
  90 bent male header
  enlarge holes here for jack

custom parts:
  Power Jack: Power Jack This is the standard 5.5mm barrel jack for power. The PTH is the most common, proven, reliable, footprint. All others are experimental. The Slot footprint only works if the mill layer is transmitted to the PCB fab house so be warned. Spark Fun Electronics SKU : PRT-00119. Mating wall wart : TOL-00298 (and others)
